// Logisim project Computadora.circ as structural Verilog: 5 circuits, main circuit main
module main (
);

  wire clock_1_out, decoder_1_out0, decoder_1_out1, decoder_1_out2, decoder_1_out3, decoder_1_out4,
       decoder_1_out5, decoder_1_out6, decoder_1_out7, decoder_2_out0, decoder_2_out1, decoder_2_out2,
       decoder_2_out3, decoder_2_out4, decoder_2_out5, decoder_2_out6, decoder_2_out7, decoder_2_out8,
       decoder_2_out9, not_1_out, not_2_out, or_1_out, or_2_out, or_3_out, or_4_out, or_5_out, or_6_out, R,
       x1, x2, x3, x4, x5, x6, x7, x8, x9, x10, x11, x12, x13, x14, x15, x16;
  wire [1:0] bit_extender_3_out;
  wire [3:0] bit_extender_2_out, T;
  wire [5:0] bit_extender_1_out, MAR, multiplexer_2_out, PC;
  wire [7:0] A, adder_1_out, B, comp_one_1_out_2, IR, load, multiplexer_1_out, multiplexer_3_out, ram_1_data;

  // Probe on T
  // Probe on PC
  // Probe on IR
  // Probe on MAR
  // Probe on load
  // Probe on A
  // Probe on B
  Button button_1 (.out(R));
  not not_1 (not_1_out, x16);
  or or_1 (or_1_out, x13, x2);
  Clock clock_1 (.out(clock_1_out));
  // Probe on 4'b0000
  // Probe on not_1_out
  Counter #(.width(4), .max('hf)) counter_1 (
    .load(x16), .D(4'b0000), .count(not_1_out), .Q(T), .clk(clock_1_out), .clr(R));  // open: carry
  Decoder #(.select(4)) decoder_1 (
    .out0(decoder_1_out0), .out1(decoder_1_out1), .out2(decoder_1_out2), .out3(decoder_1_out3),
    .out4(decoder_1_out4), .out5(decoder_1_out5), .out6(decoder_1_out6), .out7(decoder_1_out7), .sel(T));  // open: out8, out9, out10, out11, out12, out13, out14, out15, en
  RAM #(.addrWidth(6), .bus("separate")) ram_1 (
    .addr(MAR), .din(load), .data(ram_1_data), .str(x13), .sel(or_1_out), .clk(clock_1_out), .ld(x2));  // open: clr
  Bit_Extender #(.out_width(6)) bit_extender_1 (.in(load), .out(bit_extender_1_out));
  Counter #(.width(6), .max('h3f)) counter_2 (
    .load(x15), .D(bit_extender_1_out), .count(x3), .Q(PC), .clk(clock_1_out), .clr(R));  // open: carry
  Multiplexer #(.width(8)) multiplexer_1 (.in0(A), .in1(ram_1_data), .out(multiplexer_1_out), .sel(x2), .en(or_3_out));
  Multiplexer #(.width(6)) multiplexer_2 (
    .in0(bit_extender_1_out), .in1(PC), .out(multiplexer_2_out), .sel(x1));  // open: en
  or or_2 (or_2_out, x6, x1);
  or or_3 (or_3_out, x9, x2);
  Register #(.width(6)) register_1 (.D(multiplexer_2_out), .en(or_2_out), .Q(MAR), .clk(clock_1_out), .clr(R));
  Register register_2 (.D(multiplexer_1_out), .Q(load), .clk(clock_1_out), .clr(R));  // open: en
  XDecoder xdecoder_1 (
    .t0(decoder_1_out0), .t1(decoder_1_out1), .t2(decoder_1_out2), .t3(decoder_1_out3), .t4(decoder_1_out4),
    .t5(decoder_1_out5), .t6(decoder_1_out6), .t7(decoder_1_out7), .X1(x1), .X2(x2), .X3(x3), .X4(x4),
    .X5(x5), .X6(x6), .X7(x7), .X8(x8), .X9(x9), .X10(x10), .X11(x11), .X12(x12), .X13(x13), .X14(x14),
    .X15(x15), .X16(x16), .q0(decoder_2_out0), .q1(decoder_2_out1), .q2(decoder_2_out2), .q3(decoder_2_out3),
    .q4(decoder_2_out4), .q5(decoder_2_out5), .q6(decoder_2_out6), .q7(decoder_2_out7), .q8(decoder_2_out8),
    .q9(decoder_2_out9), .N(B[7]));
  or or_4 (or_4_out, decoder_1_out0, decoder_1_out1, decoder_1_out2);
  or or_5 (or_5_out, x12, R);
  Counter counter_3 (.load(x7), .D(load), .count(x14), .Q(A), .clk(clock_1_out), .clr(or_5_out));  // open: carry
  Register register_3 (.D(load), .en(x4), .Q(IR), .clk(clock_1_out), .clr(R));
  Decoder #(.select(4)) decoder_2 (
    .out0(decoder_2_out0), .out1(decoder_2_out1), .out2(decoder_2_out2), .out3(decoder_2_out3),
    .out4(decoder_2_out4), .out5(decoder_2_out5), .out6(decoder_2_out6), .out7(decoder_2_out7),
    .out8(decoder_2_out8), .out9(decoder_2_out9), .sel(bit_extender_2_out), .en(not_2_out));  // open: out10, out11, out12, out13, out14, out15
  Bit_Extender #(.out_width(4)) bit_extender_2 (.in(IR), .out(bit_extender_2_out));
  not not_2 (not_2_out, or_4_out);
  // Probe on bit_extender_3_out
  Multiplexer #(.select(2), .width(8)) multiplexer_3 (
    .in0(comp_one_1_out_2), .in1(adder_1_out), .in2(A), .out(multiplexer_3_out), .sel(bit_extender_3_out));  // open: in3, en
  Bit_Extender #(.in_width(3), .out_width(2)) bit_extender_3 (.in({x8, x5, x11}), .out(bit_extender_3_out));
  or or_6 (or_6_out, x11, x5, x8);
  Counter counter_4 (
    .load(or_6_out), .D(multiplexer_3_out), .count(x10), .Q(B), .clk(clock_1_out), .clr(R));  // open: carry
  comp_one comp_one_1 (.in_1(B), .out_2(comp_one_1_out_2));
  Adder adder_1 (.a(B), .b(A), .out(adder_1_out));  // open: cin, cout

  // Other names for the same wires on the sheet: N = B[7]; MBR[7:0] = load

  // Notes on the sheet:
  //   T
  //   PC
  //   IR
  //   MAR
  //   MBR
  //   A
  //   B
  //   Resumen de Valores
  //   BOTON RESET
  //   time decoder
  //   T (t_i)
  //   PC
  //   ENABLE
  //   READ
  //   ID
  //   MAR
  //   MBR
  //   A
  //   IR
  //   8 to 4 bits
  //   Q_i
  //   B
  //   ADDR
endmodule

module comp_one (
  input  [7:0] in_1,
  output [7:0] out_2
);

  wire [7:0] negator_1_out;

  Negator negator_1 (.in(in_1), .out(negator_1_out));
  Subtractor subtractor_1 (.a(negator_1_out), .b(8'h1), .out(out_2));  // open: bin, bout
endmodule

module controller (
);
endmodule

module addr (
  input  [3:0] in_1,
  input  [3:0] in_2,
  input  in_3,
  input  in_4,
  input  in_5,
  input  in_6,
  input  in_7,
  input  in_8,
  input  in_9,
  input  [7:0] in_10,
  input  [7:0] in_11,
  output out_12,
  output [3:0] out_13,
  output [7:0] out_14
);

  wire clock_1_out;
  wire [3:0] multiplexer_1_out, ram_1_data, register_1_q;

  Clock clock_1 (.out(clock_1_out));
  Register #(.width(4)) register_1 (.D(in_1), .Q(register_1_q), .clk(clock_1_out));  // open: en, clr
  Button button_1 (.out(in_9));
  RAM #(.addrWidth(4), .dataWidth(4)) ram_1 (
    .addr(in_2), .data(ram_1_data), .sel(in_5), .clk(clock_1_out), .ld(in_8));  // open: clr
  Multiplexer #(.width(4)) multiplexer_1 (
    .in0(register_1_q), .in1(ram_1_data), .out(multiplexer_1_out), .sel(in_4), .en(in_3));
  LED led_1 (.in(in_9));
  LED led_2 (.in(in_9));
  Register #(.width(4)) register_2 (.D(multiplexer_1_out), .Q(out_13), .clk(clock_1_out));  // open: en, clr
  // Probe on in_10
  // Probe on in_11
  Multiplexer #(.width(4)) multiplexer_2 (.in0(out_13), .out(ram_1_data), .sel(in_6), .en(in_7));  // open: in1
  Adder adder_1 (.a(in_10), .b(in_11), .out(out_14));  // open: cin, cout
  // Probe on ram_1_data
  // Probe on out_14

  assign out_12 = in_1[3];

  // Other names for the same wires on the sheet: e = in_9

  // Notes on the sheet:
  //   A
  //   mux1
  //   mbr
  //   mux2
endmodule

module XDecoder (
  input  q0,
  input  q1,
  input  q2,
  input  q3,
  input  q4,
  input  q5,
  input  q6,
  input  q7,
  input  q8,
  input  q9,
  input  N,
  input  t0,
  input  t1,
  input  t2,
  input  t3,
  input  t4,
  input  t5,
  input  t6,
  input  t7,
  output X1,
  output X2,
  output X3,
  output X4,
  output X5,
  output X6,
  output X7,
  output X8,
  output X9,
  output X10,
  output X11,
  output X12,
  output X13,
  output X14,
  output X15,
  output X16
);

  wire T3Q1_2_out, T3Q6_out, T3Q8_out, T3Q9_out, T4Q1_out, T4Q6_out, T4Q8_out, T4Q9_out, T5Q1_out, T5Q6_out,
       T5Q8_out, T5Q9_out, T5Q9N_out, T6Q1_out;

  and T3Q1 (X5, q0, t3);
  and T3Q1_2 (T3Q1_2_out, q1, t3);
  and T4Q1 (T4Q1_out, q1, t4);
  and T5Q1 (T5Q1_out, q1, t5);
  and T6Q1 (T6Q1_out, q1, t6);
  and T7Q1 (X7, q1, t7);
  and T3Q2 (X8, q2, t3);
  and T3Q3 (X10, q3, t3);
  and T3Q4 (X11, q4, t3);
  and T3Q5 (X12, q5, t3);
  and T3Q6 (T3Q6_out, q6, t3);
  and T4Q6 (T4Q6_out, q6, t4);
  and T5Q6 (T5Q6_out, q6, t5);
  and T6Q6 (X9, q6, t6);
  and T7Q6 (X13, q6, t7);
  and T3Q7 (X14, q7, t3);
  and T3Q8 (T3Q8_out, q8, t3);
  and T4Q8 (T4Q8_out, q8, t4);
  and T5Q8 (T5Q8_out, q8, t5);
  and T3Q9 (T3Q9_out, q9, t3);
  and T4Q9 (T4Q9_out, q9, t4);
  and T5Q9 (T5Q9_out, q9, t5);
  and T5Q9N (T5Q9N_out, N, T5Q9_out);
  or u_X1 (X1, t0, T3Q1_2_out, T3Q6_out, T3Q8_out, T3Q9_out);
  or u_X2 (X2, T4Q1_out, T4Q6_out, t1, T6Q1_out, T4Q8_out, T4Q9_out);
  or u_X3 (X3, T4Q1_out, t1, T4Q6_out, T4Q9_out);
  or X3_2 (X6, T5Q1_out, T5Q6_out);
  or u_X15 (X15, T5Q8_out, T5Q9N_out);
  or u_X16 (X16, T5Q9_out, T5Q8_out, X14, X13, X12, X11, X10, X8, X7, X5);

  assign X4 = t2;

  // Notes on the sheet:
  //   TIEMPOS
  //   t2
  //   T1
endmodule
